# Fritzing sketch ble-gps-nodemcu (saved by Fritzing 0.9.3b)
perfboards: 1

parts:
  J12 = female pin header, 3 pins [form="♀ (female)"]
  GY-NEO6MV3 = SUP500F [package=sup500f]
  U1 = NodeMCU V1.0
  J13 = female pin header, 3 pins [form="♀ (female)"]
  J14 = female pin header, 3 pins [form="♀ (female)"]
  Part1 = Bluetooth HM-10

nets:
  3V3: J12.pin1, GY-NEO6MV3.PSEL, U1.3V3, J14.pin2, Part1.VCC
  GND: J12.pin2, GY-NEO6MV3.PPS, U1.GND, J14.pin1, Part1.GND
  N1: J12.pin3, GY-NEO6MV3.VBAT, U1.D2
  N2: U1.D1, J13.pin3

custom parts:
  NodeMCU V1.0: ESP8266 based NodeMCU
